// Logisim project print_ADXL345_values.circ as structural Verilog: 3 circuits, main circuit print_accel_values
module print_accel_values (
  input  rst,
  input  miso,
  input  accel_input,
  input  enable_accel,
  output mosi,
  output sclk,
  output cs
);

  wire [1:0] SELECTOR;
  wire [3:0] multiplexer_1_out, multiplexer_2_out, multiplexer_3_out, multiplexer_4_out;
  wire [47:0] accel_main_driver_1_accelerometer;

  DipSwitch #(.number(2)) AXIS_SELECTOR (.sw1(SELECTOR[0]), .sw2(SELECTOR[1]));
  accel_main_driver accel_main_driver_1 (
    .rst(rst), .miso(miso), .accel_input(accel_input), .enable_accel(enable_accel), .mosi(mosi), .sclk(sclk),
    .cs(cs), .Accelerometer(accel_main_driver_1_accelerometer));
  Multiplexer #(.select(2), .width(4)) multiplexer_1 (
    .in0(accel_main_driver_1_accelerometer[3:0]), .in1(accel_main_driver_1_accelerometer[19:16]),
    .in2(accel_main_driver_1_accelerometer[35:32]), .out(multiplexer_1_out), .sel(SELECTOR));  // open: in3
  sevenseg_accel_output HEX0 (.Input_bus_1(multiplexer_1_out));
  Multiplexer #(.select(2), .width(4)) multiplexer_2 (
    .in0(accel_main_driver_1_accelerometer[7:4]), .in1(accel_main_driver_1_accelerometer[23:20]),
    .in2(accel_main_driver_1_accelerometer[39:36]), .out(multiplexer_2_out), .sel(SELECTOR));  // open: in3
  sevenseg_accel_output HEX1 (.Input_bus_1(multiplexer_2_out));
  Multiplexer #(.select(2), .width(4)) multiplexer_3 (
    .in0(accel_main_driver_1_accelerometer[11:8]), .in1(accel_main_driver_1_accelerometer[27:24]),
    .in2(accel_main_driver_1_accelerometer[43:40]), .out(multiplexer_3_out), .sel(SELECTOR));  // open: in3
  sevenseg_accel_output HEX2 (.Input_bus_1(multiplexer_3_out));
  Multiplexer #(.select(2), .width(4)) multiplexer_4 (
    .in0(accel_main_driver_1_accelerometer[15:12]), .in1(accel_main_driver_1_accelerometer[31:28]),
    .in2(accel_main_driver_1_accelerometer[47:44]), .out(multiplexer_4_out), .sel(SELECTOR));  // open: in3
  sevenseg_accel_output HEX3 (.Input_bus_1(multiplexer_4_out));

  // Notes on the sheet:
  //   PRINT_ADXL345_VALUES
  //   00: X-AXIS
  //   01: Y-AXIS
  //   10: Z-AXIS
  //   THE "AXES_SELECTOR" ALLOWS US TO SWITCH BETWEEN THE DIFFERENT AXES
  //   OUTPUTS ON 4 HEXES THE VALUES OF THE ACCELERATION ON THE DIFFERENT AXES OF THE ACCELEROMETER
endmodule

module sevenseg_accel_logic (
  input  [3:0] accel,
  output [7:0] sevensegment
);

  wire and_1_out, and_2_out, and_3_out, and_4_out, and_5_out, and_6_out, and_7_out, and_8_out, and_9_out,
       and_10_out, and_11_out, and_12_out, and_13_out, and_14_out, and_15_out, and_16_out, and_17_out,
       and_18_out, and_19_out, and_20_out, and_21_out, and_22_out, and_23_out, and_24_out, and_25_out,
       and_26_out, and_27_out, and_28_out, and_29_out, and_30_out, and_31_out, and_32_out, and_33_out,
       and_34_out, and_35_out, and_36_out, not_1_out, not_2_out, not_3_out, not_4_out;

  not not_1 (not_1_out, accel[3]);
  not not_2 (not_2_out, accel[2]);
  not not_3 (not_3_out, accel[1]);
  not not_4 (not_4_out, accel[0]);
  and and_1 (and_1_out, not_2_out, accel[1]);
  and and_2 (and_2_out, accel[1], not_4_out);
  and and_3 (and_3_out, not_1_out, accel[2], not_3_out);
  and and_4 (and_4_out, accel[3], not_2_out);
  and and_5 (and_5_out, accel[3], accel[0]);
  and and_6 (and_6_out, not_3_out, not_4_out);
  and and_7 (and_7_out, not_1_out, accel[2], not_3_out);
  and and_8 (and_8_out, accel[2], not_4_out);
  and and_9 (and_9_out, accel[3], not_2_out);
  and and_10 (and_10_out, accel[3], accel[1]);
  and and_11 (and_11_out, not_2_out, not_4_out);
  and and_12 (and_12_out, accel[1], not_4_out);
  and and_13 (and_13_out, accel[3], accel[1]);
  and and_14 (and_14_out, accel[3], accel[2]);
  and and_15 (and_15_out, not_1_out, not_2_out, not_4_out);
  and and_16 (and_16_out, not_1_out, accel[1], not_4_out);
  and and_17 (and_17_out, not_2_out, accel[1], accel[0]);
  and and_18 (and_18_out, accel[2], not_3_out, accel[0]);
  and and_19 (and_19_out, accel[3], not_3_out);
  and and_20 (and_20_out, accel[3], accel[2], not_4_out);
  and and_21 (and_21_out, not_1_out, not_3_out);
  and and_22 (and_22_out, not_1_out, accel[0]);
  and and_23 (and_23_out, not_3_out, accel[0]);
  and and_24 (and_24_out, not_1_out, accel[2]);
  and and_25 (and_25_out, accel[3], not_2_out);
  and and_26 (and_26_out, not_1_out, not_2_out);
  and and_27 (and_27_out, not_1_out, not_3_out, not_4_out);
  and and_28 (and_28_out, not_2_out, not_4_out);
  and and_29 (and_29_out, not_1_out, accel[1], accel[0]);
  and and_30 (and_30_out, accel[3], not_3_out, accel[0]);
  and and_31 (and_31_out, not_2_out, not_4_out);
  and and_32 (and_32_out, not_1_out, accel[1]);
  and and_33 (and_33_out, not_1_out, accel[2], accel[0]);
  and and_34 (and_34_out, accel[2], accel[1]);
  and and_35 (and_35_out, accel[3], not_2_out, not_3_out);
  and and_36 (and_36_out, accel[3], not_4_out);
  or or_1 (sevensegment[6], and_1_out, and_2_out, and_3_out, and_4_out, and_5_out);
  or or_2 (sevensegment[5], and_6_out, and_7_out, and_8_out, and_9_out, and_10_out);
  or or_3 (sevensegment[4], and_11_out, and_12_out, and_13_out, and_14_out);
  or or_4 (sevensegment[3], and_15_out, and_16_out, and_17_out, and_18_out, and_19_out, and_20_out);
  or or_5 (sevensegment[2], and_21_out, and_22_out, and_23_out, and_24_out, and_25_out);
  or or_6 (sevensegment[1], and_26_out, and_27_out, and_28_out, and_29_out, and_30_out);
  or or_7 (sevensegment[0], and_31_out, and_32_out, and_33_out, and_34_out, and_35_out, and_36_out);

  assign sevensegment[7] = 1'b0;
endmodule

module sevenseg_accel_output (
  input  [3:0] Input_bus_1
);

  wire [7:0] sevenseg_1_sevensegment;

  sevenseg_accel_logic sevenseg_1 (.accel(Input_bus_1), .sevensegment(sevenseg_1_sevensegment));
  _7_Segment_Display L_7_Segment_Display_1 (
    .g(sevenseg_1_sevensegment[6]), .f(sevenseg_1_sevensegment[5]), .a(sevenseg_1_sevensegment[0]),
    .b(sevenseg_1_sevensegment[1]), .e(sevenseg_1_sevensegment[4]), .d(sevenseg_1_sevensegment[3]),
    .c(sevenseg_1_sevensegment[2]), .dp(sevenseg_1_sevensegment[7]));
endmodule
